# Fritzing sketch Circuits (saved by Fritzing 0.9.3b)
breadboards: 1

parts:
  Part1 = Arduino Nano (Rev3.0)
  U3 = NodeMCU V3.0
  DHT1 = dht11
  electronicsguy1 = electronicsguy 0.96" 128x64 SPI I2C OLED

nets:
  GND: Part1.GND, U3.GND, DHT1.connector10, electronicsguy1.GND
  N1: Part1.D2, electronicsguy1.D0
  N2: Part1.D3, electronicsguy1.D1
  N3: Part1.D4, electronicsguy1.RST
  N4: Part1.D5, U3.D2
  N5: Part1.D6, U3.D1
  N6: Part1.D7, electronicsguy1.DC
  N7: Part1.D8, electronicsguy1.CS
  5V: Part1.5V, electronicsguy1.VCC
  N8: U3.D5, DHT1.connector9
  N9: U3.VU, DHT1.connector8

custom parts:
  NodeMCU V3.0: ESP8266 based NodeMCU
  electronicsguy 0.96" 128x64 SPI I2C OLED: Generic 0.96" 128x64 SPI I2C OLED Default is SPI mode Can be re-configured for I2C (needs soldering work) Comes in various colors like blue, white, yellow-blue
