# Fritzing sketch Actuator_unit (saved by Fritzing 0.9.3b)
breadboards: 1

parts:
  KY-1 = Keyes Relay [part_number="Relay modul 1ch (low lewel trigger)" package=THT]
  Q1 = NPN-Transistor [package="TO92 [THT]"]
  R1 = Resistor [tolerance=±5% resistance=330 package=THT]
  R2 = Resistor [tolerance=±5% resistance=10k package=THT]
  WeMos_D1_Mini_Lite1 = WeMos D1 Mini Lite

nets:
  N1: KY-1.NC, WeMos_D1_Mini_Lite1.5V
  N2: KY-1.NO, Q1.E, Q1.C, R2.Pin_1, WeMos_D1_Mini_Lite1.G
  N3: Q1.B, R1.Pin_1, R2.Pin_0
  N4: R1.Pin_0, WeMos_D1_Mini_Lite1.D2
  Factory actuator's relay pin1: WeMos_D1_Mini_Lite1.A0
  Factory actuator's relay pin2: WeMos_D1_Mini_Lite1.D0

custom parts:
  Keyes Relay: The Keyes 5V relay module is suitable for SCM development, home appliance control. It uses a 5V~12V TIL control signal which can control DC / AC signal.
  WeMos D1 Mini Lite: A simple wifi board with 1MB flash based on ESP-8285
